// Logisim project snake_game_final.circ as structural Verilog: 1 circuit, main circuit main
module main (
);

  wire and_1_out, and_2_out, and_3_out, and_4_out, and_5_out, and_6_out, and_7_out, and_8_out, and_9_out,
       and_10_out, Aup, available, Bup, CLK, clock_1_out, comparator_1_gt, comparator_2_gt, comparator_3_gt,
       comparator_4_gt, comparator_5_eq, comparator_6_eq, comparator_11_eq, comparator_12_eq,
       comparator_13_eq, comparator_14_eq, comparator_15_eq, comparator_16_eq, comparator_17_eq,
       comparator_18_eq, comparator_19_eq, comparator_20_eq, comparator_21_eq, comparator_22_eq,
       comparator_23_eq, comparator_24_eq, comparator_25_eq, comparator_26_eq, comparator_27_eq,
       controlled_buffer_1_out, Cup, Dup, multiplexer_1_out, not_1_out, not_2_out, not_3_out, not_4_out,
       not_5_out, not_6_out, or_1_out, or_15_out, or_19_out;
  wire [1:0] tunnel;
  wire [3:0] adder_1_out, adder_2_out, adder_3_out, AppX, AppY, AXPos, AYPos, bit_extender_1_out,
       bit_extender_6_out, BXPos, BYPos, CXPos, CYPos, direction, directionChange, DXPos, DYPos, HeadXPos,
       HeadYPos, multiplexer_2_out, multiplexer_3_out, multiplexer_16_out, multiplexer_25_out, Rand0,
       random_1_out, random_2_out, State, subtractor_1_out, subtractor_2_out;
  wire [4:0] bit_extender_2_out, bit_extender_3_out, bit_extender_4_out, bit_extender_5_out,
       multiplexer_8_out, multiplexer_9_out, multiplexer_10_out, multiplexer_11_out;
  wire [6:0] value;
  wire [15:0] _00, _01, _02, _03, _04, _05, _06, _07, _08, _09, _010, _011, _012, _013, _014, _015, A0, A1,
       A2, A3, A4, A5, A6, A7, A8, A9, A10, A11, A12, A13, A14, A15, AYOut, B0, B1, B2, B3, B4, B5, B6, B7,
       B8, B9, B10, B11, B12, B13, B14, B15, BYOut, C0, C1, C2, C3, C4, C5, C6, C7, C8, C9, C10, C11, C12,
       C13, C14, C15, CYOut, D0, D1, D2, D3, D4, D5, D6, D7, D8, D9, D10, D11, D12, D13, D14, D15,
       decoder_6_out0, DYOut, HeadYOut, n0, n1, n2, n3, n4, n5, n6, n7, n8, n9, n10, n11, n12, n13, n14, n15,
       P0, P1, P2, P3, P4, P5, P6, P7, P8, P9, P10, P11, P12, P13, P14, P15, Z0, Z1, Z2, Z3, Z4, Z5, Z6, Z7,
       Z8, Z9, Z10, Z11, Z12, Z13, Z14, Z15;

  DotMatrix #(.matrixcols(16), .matrixrows(16)) dotmatrix_1 (
    .col0(n0), .col1(n1), .col2(n2), .col3(n3), .col4(n4), .col5(n5), .col6(n6), .col7(n7), .col8(n8),
    .col9(n9), .col10(n10), .col11(n11), .col12(n12), .col13(n13), .col14(n14), .col15(n15));
  Keyboard keyboard_1 (.clk(controlled_buffer_1_out), .avail(available), .data(value));  // open: re, clr
  assign controlled_buffer_1_out = available ? CLK : 1'bz;  // Controlled_Buffer controlled_buffer_1
  Register #(.width(4)) u_State (.D(adder_1_out), .Q(State), .clk(CLK));  // open: en, clr
  Multiplexer #(.select(4), .enable("false")) multiplexer_1 (
    .in0(1'b1), .in1(1'b0), .in2(1'b1), .in3(1'b0), .in4(1'b1), .in5(1'b0), .in6(1'b1), .in7(1'b0),
    .in8(1'b1), .in9(1'b0), .out(multiplexer_1_out), .sel(State));  // open: in10, in11, in12, in13, in14, in15
  assign bit_extender_1_out = {{3{1'b0}}, multiplexer_1_out};  // Bit_Extender bit_extender_1
  Comparator #(.width(4), .mode("unsigned")) comparator_1 (
    .a(State), .b(4'b0001), .gt(comparator_1_gt));  // open: eq, lt
  Comparator #(.width(4), .mode("unsigned")) comparator_2 (
    .a(State), .b(4'b0011), .gt(comparator_2_gt));  // open: eq, lt
  Comparator #(.width(4), .mode("unsigned")) comparator_3 (
    .a(State), .b(4'b0101), .gt(comparator_3_gt));  // open: eq, lt
  Comparator #(.width(4), .mode("unsigned")) comparator_4 (
    .a(State), .b(4'b0111), .gt(comparator_4_gt));  // open: eq, lt
  Register #(.width(4)) u_AppX (.D(Rand0), .en(multiplexer_1_out), .Q(AppX), .clk(CLK));  // open: clr
  Random #(.width(4)) random_1 (.clk(CLK), .out(random_1_out));  // open: next, clr
  Adder #(.width(4)) adder_1 (.a(bit_extender_1_out), .b(State), .out(adder_1_out), .cin(and_1_out));  // open: cout
  Decoder #(.select(4), .enable("false")) decoder_1 (
    .out0(HeadYOut[0]), .out1(HeadYOut[1]), .out2(HeadYOut[2]), .out3(HeadYOut[3]), .out4(HeadYOut[4]),
    .out5(HeadYOut[5]), .out6(HeadYOut[6]), .out7(HeadYOut[7]), .out8(HeadYOut[8]), .out9(HeadYOut[9]),
    .out10(HeadYOut[10]), .out11(HeadYOut[11]), .out12(HeadYOut[12]), .out13(HeadYOut[13]),
    .out14(HeadYOut[14]), .out15(HeadYOut[15]), .sel(HeadYPos));
  Register #(.width(4)) AY (.D(HeadYPos), .en(comparator_1_gt), .Q(AYPos), .clk(CLK));  // open: clr
  Decoder #(.select(4), .enable("false")) decoder_2 (
    .out0(AYOut[0]), .out1(AYOut[1]), .out2(AYOut[2]), .out3(AYOut[3]), .out4(AYOut[4]), .out5(AYOut[5]),
    .out6(AYOut[6]), .out7(AYOut[7]), .out8(AYOut[8]), .out9(AYOut[9]), .out10(AYOut[10]), .out11(AYOut[11]),
    .out12(AYOut[12]), .out13(AYOut[13]), .out14(AYOut[14]), .out15(AYOut[15]), .sel(AYPos));
  Register #(.width(4)) BY (.D(AYPos), .en(comparator_2_gt), .Q(BYPos), .clk(CLK));  // open: clr
  Decoder #(.select(4), .enable("false")) decoder_3 (
    .out0(BYOut[0]), .out1(BYOut[1]), .out2(BYOut[2]), .out3(BYOut[3]), .out4(BYOut[4]), .out5(BYOut[5]),
    .out6(BYOut[6]), .out7(BYOut[7]), .out8(BYOut[8]), .out9(BYOut[9]), .out10(BYOut[10]), .out11(BYOut[11]),
    .out12(BYOut[12]), .out13(BYOut[13]), .out14(BYOut[14]), .out15(BYOut[15]), .sel(BYPos));
  Register #(.width(4)) CY (.D(BYPos), .en(comparator_3_gt), .Q(CYPos), .clk(CLK));  // open: clr
  Decoder #(.select(4), .enable("false")) decoder_4 (
    .out0(CYOut[0]), .out1(CYOut[1]), .out2(CYOut[2]), .out3(CYOut[3]), .out4(CYOut[4]), .out5(CYOut[5]),
    .out6(CYOut[6]), .out7(CYOut[7]), .out8(CYOut[8]), .out9(CYOut[9]), .out10(CYOut[10]), .out11(CYOut[11]),
    .out12(CYOut[12]), .out13(CYOut[13]), .out14(CYOut[14]), .out15(CYOut[15]), .sel(CYPos));
  Register #(.width(4)) DY (.D(CYPos), .en(comparator_4_gt), .Q(DYPos), .clk(CLK));  // open: clr
  Decoder #(.select(4), .enable("false")) decoder_5 (
    .out0(DYOut[0]), .out1(DYOut[1]), .out2(DYOut[2]), .out3(DYOut[3]), .out4(DYOut[4]), .out5(DYOut[5]),
    .out6(DYOut[6]), .out7(DYOut[7]), .out8(DYOut[8]), .out9(DYOut[9]), .out10(DYOut[10]), .out11(DYOut[11]),
    .out12(DYOut[12]), .out13(DYOut[13]), .out14(DYOut[14]), .out15(DYOut[15]), .sel(DYPos));
  Demultiplexer #(.select(4), .width(16), .enable("false")) demultiplexer_1 (
    .out0(P0), .out1(P1), .out2(P2), .out3(P3), .out4(P4), .out5(P5), .out6(P6), .out7(P7), .out8(P8),
    .out9(P9), .out10(P10), .out11(P11), .out12(P12), .out13(P13), .out14(P14), .out15(P15),
    .in(decoder_6_out0), .sel(AppX));
  Register #(.width(4)) u_AppY (.D(random_1_out), .en(multiplexer_1_out), .Q(AppY), .clk(CLK));  // open: clr
  not not_1 (not_1_out, multiplexer_1_out);
  Multiplexer #(.select(4), .width(4), .enable("false")) multiplexer_2 (
    .in0(4'b0111), .in1(multiplexer_3_out), .in2(multiplexer_3_out), .in3(multiplexer_3_out),
    .in4(multiplexer_3_out), .in5(multiplexer_3_out), .in6(multiplexer_3_out), .in7(multiplexer_3_out),
    .in8(multiplexer_3_out), .in9(multiplexer_3_out), .out(multiplexer_2_out), .sel(State));  // open: in10, in11, in12, in13, in14, in15
  Decoder #(.select(4), .enable("false")) decoder_6 (
    .out0(decoder_6_out0[0]), .out1(decoder_6_out0[1]), .out2(decoder_6_out0[2]), .out3(decoder_6_out0[3]),
    .out4(decoder_6_out0[4]), .out5(decoder_6_out0[5]), .out6(decoder_6_out0[6]), .out7(decoder_6_out0[7]),
    .out8(decoder_6_out0[8]), .out9(decoder_6_out0[9]), .out10(decoder_6_out0[10]),
    .out11(decoder_6_out0[11]), .out12(decoder_6_out0[12]), .out13(decoder_6_out0[13]),
    .out14(decoder_6_out0[14]), .out15(decoder_6_out0[15]), .sel(AppY));
  Comparator #(.width(4)) comparator_5 (.a(HeadXPos), .b(AppX), .eq(comparator_5_eq));  // open: gt, lt
  Comparator #(.width(4)) comparator_6 (.a(HeadYPos), .b(AppY), .eq(comparator_6_eq));  // open: gt, lt
  Register #(.width(4)) HeadX (.D(multiplexer_2_out), .Q(HeadXPos), .clk(CLK));  // open: en, clr
  and and_1 (and_1_out, comparator_5_eq, comparator_6_eq, not_1_out);
  Subtractor #(.width(4)) subtractor_1 (.a(HeadXPos), .b(4'b0001), .out(subtractor_1_out));  // open: bin, bout
  Adder #(.width(4)) adder_2 (.a(HeadXPos), .b(4'b0001), .out(adder_2_out));  // open: cin, cout
  Multiplexer #(.select(4), .width(4), .enable("false")) multiplexer_3 (
    .in1(subtractor_1_out), .in4(adder_2_out), .out(multiplexer_3_out), .sel(directionChange));  // open: in0, in2, in3, in5, in6, in7, in8, in9, in10, in11, in12, in13, in14, in15
  Comparator #(.width(4), .mode("unsigned")) comparator_7 (.a(State), .b(4'b1000), .gt(Dup));  // open: eq, lt
  Comparator #(.width(4), .mode("unsigned")) comparator_8 (.a(State), .b(4'b0110), .gt(Cup));  // open: eq, lt
  Comparator #(.width(4), .mode("unsigned")) comparator_9 (.a(State), .b(4'b0100), .gt(Bup));  // open: eq, lt
  Comparator #(.width(4), .mode("unsigned")) comparator_10 (.a(State), .b(4'b0010), .gt(Aup));  // open: eq, lt
  Multiplexer #(.select(2), .width(16), .enable("false")) multiplexer_4 (
    .in0(Z0), .in1({16{1'b0}}), .in2({16{1'b0}}), .in3({16{1'b0}}), .out(n0), .sel(tunnel));
  Multiplexer #(.select(2), .width(16), .enable("false")) multiplexer_5 (
    .in0(Z1), .in1(16'h3c0), .in2(16'h3c0), .in3(16'h3c0), .out(n1), .sel(tunnel));
  Multiplexer #(.select(2), .width(16), .enable("false")) multiplexer_6 (
    .in0(Z2), .in1(16'hc30), .in2(16'hc30), .in3(16'hc30), .out(n2), .sel(tunnel));
  Multiplexer #(.select(2), .width(16), .enable("false")) multiplexer_7 (
    .in0(Z3), .in1(16'h1008), .in2(16'h1008), .in3(16'h1008), .out(n3), .sel(tunnel));
  Register #(.width(4)) CX (.D(CXPos), .Q(DXPos), .clk(CLK));  // open: en, clr
  Register #(.width(4)) CX_2 (.D(BXPos), .Q(CXPos), .clk(CLK));  // open: en, clr
  Register #(.width(4)) BX (.D(AXPos), .Q(BXPos), .clk(CLK));  // open: en, clr
  Register #(.width(4)) AX (.D(HeadXPos), .Q(AXPos), .clk(CLK));  // open: en, clr
  assign bit_extender_2_out = {{1{1'b0}}, DXPos};  // Bit_Extender bit_extender_2
  assign bit_extender_3_out = {{1{1'b0}}, CXPos};  // Bit_Extender bit_extender_3
  assign bit_extender_4_out = {{1{1'b0}}, BXPos};  // Bit_Extender bit_extender_4
  assign bit_extender_5_out = {{1{1'b0}}, AXPos};  // Bit_Extender bit_extender_5
  Multiplexer #(.width(5), .enable("false")) multiplexer_8 (
    .in0(5'b10001), .in1(bit_extender_2_out), .out(multiplexer_8_out), .sel(Dup));
  Multiplexer #(.width(5), .enable("false")) multiplexer_9 (
    .in0(5'b10001), .in1(bit_extender_3_out), .out(multiplexer_9_out), .sel(Cup));
  Multiplexer #(.width(5), .enable("false")) multiplexer_10 (
    .in0(5'b10001), .in1(bit_extender_4_out), .out(multiplexer_10_out), .sel(Bup));
  Multiplexer #(.width(5), .enable("false")) multiplexer_11 (
    .in0(5'b10001), .in1(bit_extender_5_out), .out(multiplexer_11_out), .sel(Aup));
  Multiplexer #(.select(2), .width(16), .enable("false")) multiplexer_12 (
    .in0(Z4), .in1(16'h2264), .in2(16'h2434), .in3(16'h2264), .out(n4), .sel(tunnel));
  Multiplexer #(.select(2), .width(16), .enable("false")) multiplexer_13 (
    .in0(Z5), .in1(16'h2414), .in2(16'h2244), .in3(16'h2414), .out(n5), .sel(tunnel));
  Multiplexer #(.select(2), .width(16), .enable("false")) multiplexer_14 (
    .in0(Z6), .in1(16'h4212), .in2(16'h4482), .in3(16'h4212), .out(n6), .sel(tunnel));
  Multiplexer #(.select(2), .width(16), .enable("false")) multiplexer_15 (
    .in0(Z7), .in1(16'h4012), .in2(16'h4082), .in3(16'h4012), .out(n7), .sel(tunnel));
  Comparator #(.width(7), .mode("unsigned")) comparator_11 (
    .a(value), .b(7'b1100001), .eq(comparator_11_eq));  // open: gt, lt
  Comparator #(.width(4), .mode("unsigned")) comparator_12 (
    .a(direction), .b(4'b0100), .eq(comparator_12_eq));  // open: gt, lt
  not not_2 (not_2_out, comparator_12_eq);
  Comparator #(.width(7), .mode("unsigned")) comparator_13 (
    .a(value), .b(7'b1100100), .eq(comparator_13_eq));  // open: gt, lt
  not not_3 (not_3_out, comparator_14_eq);
  Comparator #(.width(4), .mode("unsigned")) comparator_14 (
    .a(direction), .b(4'b0001), .eq(comparator_14_eq));  // open: gt, lt
  Comparator #(.width(7), .mode("unsigned")) comparator_15 (
    .a(value), .b(7'b1110011), .eq(comparator_15_eq));  // open: gt, lt
  not not_4 (not_4_out, comparator_16_eq);
  Comparator #(.width(4), .mode("unsigned")) comparator_16 (
    .a(direction), .b(4'b0111), .eq(comparator_16_eq));  // open: gt, lt
  Comparator #(.width(7), .mode("unsigned")) comparator_17 (
    .a(value), .b(7'b1110111), .eq(comparator_17_eq));  // open: gt, lt
  not not_5 (not_5_out, comparator_18_eq);
  Comparator #(.width(4), .mode("unsigned")) comparator_18 (
    .a(direction), .b(4'b0011), .eq(comparator_18_eq));  // open: gt, lt
  Multiplexer #(.select(4), .width(4), .enable("false")) multiplexer_16 (
    .in0(4'b1000), .in1(multiplexer_25_out), .in2(multiplexer_25_out), .in3(multiplexer_25_out),
    .in4(multiplexer_25_out), .in5(multiplexer_25_out), .in6(multiplexer_25_out), .in7(multiplexer_25_out),
    .in8(multiplexer_25_out), .in9(multiplexer_25_out), .out(multiplexer_16_out), .sel(State));  // open: in10, in11, in12, in13, in14, in15
  Multiplexer #(.select(2), .width(16), .enable("false")) multiplexer_17 (
    .in0(Z8), .in1(16'h4012), .in2(16'h4082), .in3(16'h4012), .out(n8), .sel(tunnel));
  Multiplexer #(.select(2), .width(16), .enable("false")) multiplexer_18 (
    .in0(Z9), .in1(16'h4212), .in2(16'h4482), .in3(16'h4212), .out(n9), .sel(tunnel));
  Multiplexer #(.select(2), .width(16), .enable("false")) multiplexer_19 (
    .in0(Z10), .in1(16'h2414), .in2(16'h2244), .in3(16'h2414), .out(n10), .sel(tunnel));
  Multiplexer #(.select(2), .width(16), .enable("false")) multiplexer_20 (
    .in0(Z11), .in1(16'h2264), .in2(16'h2434), .in3(16'h2264), .out(n11), .sel(tunnel));
  and and_2 (and_2_out, comparator_11_eq, not_2_out);
  and and_3 (and_3_out, comparator_13_eq, not_3_out);
  and and_4 (and_4_out, comparator_15_eq, not_4_out);
  and and_5 (and_5_out, comparator_17_eq, not_5_out);
  Bit_Extender #(.in_width(7), .out_width(4)) bit_extender_6 (.in(value), .out(bit_extender_6_out));
  Register #(.width(4)) HeadY (.D(multiplexer_16_out), .Q(HeadYPos), .clk(CLK));  // open: en, clr
  Demultiplexer #(.select(5), .width(16), .enable("false")) demultiplexer_2 (
    .out0(D0), .out1(D1), .out2(D2), .out3(D3), .out4(D4), .out5(D5), .out6(D6), .out7(D7), .out8(D8),
    .out9(D9), .out10(D10), .out11(D11), .out12(D12), .out13(D13), .out14(D14), .out15(D15), .in(DYOut),
    .sel(multiplexer_8_out));  // open: out16, out17, out18, out19, out20, out21, out22, out23, out24, out25, out26, out27, out28, out29, out30, out31
  Demultiplexer #(.select(5), .width(16), .enable("false")) demultiplexer_3 (
    .out0(C0), .out1(C1), .out2(C2), .out3(C3), .out4(C4), .out5(C5), .out6(C6), .out7(C7), .out8(C8),
    .out9(C9), .out10(C10), .out11(C11), .out12(C12), .out13(C13), .out14(C14), .out15(C15), .in(CYOut),
    .sel(multiplexer_9_out));  // open: out16, out17, out18, out19, out20, out21, out22, out23, out24, out25, out26, out27, out28, out29, out30, out31
  Demultiplexer #(.select(5), .width(16), .enable("false")) demultiplexer_4 (
    .out0(B0), .out1(B1), .out2(B2), .out3(B3), .out4(B4), .out5(B5), .out6(B6), .out7(B7), .out8(B8),
    .out9(B9), .out10(B10), .out11(B11), .out12(B12), .out13(B13), .out14(B14), .out15(B15), .in(BYOut),
    .sel(multiplexer_10_out));  // open: out16, out17, out18, out19, out20, out21, out22, out23, out24, out25, out26, out27, out28, out29, out30, out31
  Demultiplexer #(.select(5), .width(16), .enable("false")) demultiplexer_5 (
    .out0(A0), .out1(A1), .out2(A2), .out3(A3), .out4(A4), .out5(A5), .out6(A6), .out7(A7), .out8(A8),
    .out9(A9), .out10(A10), .out11(A11), .out12(A12), .out13(A13), .out14(A14), .out15(A15), .in(AYOut),
    .sel(multiplexer_11_out));  // open: out16, out17, out18, out19, out20, out21, out22, out23, out24, out25, out26, out27, out28, out29, out30, out31
  or or_1 (or_1_out, and_2_out, and_3_out, and_4_out, and_5_out);
  Subtractor #(.width(4)) subtractor_2 (.a(HeadYPos), .b(4'b0001), .out(subtractor_2_out));  // open: bin, bout
  Adder #(.width(4)) adder_3 (.a(HeadYPos), .b(4'b0001), .out(adder_3_out));  // open: cin, cout
  Multiplexer #(.select(2), .width(16), .enable("false")) multiplexer_21 (
    .in0(Z12), .in1(16'h1008), .in2(16'h1008), .in3(16'h1008), .out(n12), .sel(tunnel));
  Multiplexer #(.select(2), .width(16), .enable("false")) multiplexer_22 (
    .in0(Z13), .in1(16'hc30), .in2(16'hc30), .in3(16'hc30), .out(n13), .sel(tunnel));
  Multiplexer #(.select(2), .width(16), .enable("false")) multiplexer_23 (
    .in0(Z14), .in1(16'h3c0), .in2(16'h3c0), .in3(16'h3c0), .out(n14), .sel(tunnel));
  Multiplexer #(.select(2), .width(16), .enable("false")) multiplexer_24 (
    .in0(Z15), .in1({16{1'b0}}), .in2({16{1'b0}}), .in3({16{1'b0}}), .out(n15), .sel(tunnel));
  and and_6 (and_6_out, or_1_out, available);
  Multiplexer #(.select(4), .width(4), .enable("false")) multiplexer_25 (
    .in3(subtractor_2_out), .in7(adder_3_out), .out(multiplexer_25_out), .sel(directionChange));  // open: in0, in1, in2, in4, in5, in6, in8, in9, in10, in11, in12, in13, in14, in15
  Register #(.width(4)) u_direction (.D(directionChange), .Q(direction), .clk(CLK));  // open: en, clr
  Multiplexer #(.width(4), .enable("false")) multiplexer_26 (
    .in0(direction), .in1(bit_extender_6_out), .out(directionChange), .sel(and_6_out));
  Demultiplexer #(.select(4), .width(16), .enable("false")) demultiplexer_6 (
    .out0(_00), .out1(_01), .out2(_02), .out3(_03), .out4(_04), .out5(_05), .out6(_06), .out7(_07),
    .out8(_08), .out9(_09), .out10(_010), .out11(_011), .out12(_012), .out13(_013), .out14(_014),
    .out15(_015), .in(HeadYOut), .sel(HeadXPos));
  Multiplexer #(.select(4), .width(4), .enable("false")) multiplexer_27 (
    .in0(4'b0000), .in1(4'b0001), .in2(4'b0010), .in3(4'b0011), .in4(4'b0100), .in5(4'b0101), .in6(4'b0110),
    .in7(4'b0111), .in8(4'b1000), .in9(4'b1001), .in10(4'b1010), .in11(4'b1011), .in12(4'b1100),
    .in13(4'b1101), .in14(4'b1110), .in15(4'b1111), .out(Rand0), .sel(random_2_out));
  Random #(.width(4)) random_2 (.clk(CLK), .out(random_2_out));  // open: next, clr
  assign Z0 = _00 | A0 | B0 | C0 | D0 | P0;  // OR_Gate or_2, 16 bits wide
  assign Z4 = _04 | A4 | B4 | C4 | D4 | P4;  // OR_Gate or_3, 16 bits wide
  assign Z8 = _08 | A8 | B8 | C8 | D8 | P8;  // OR_Gate or_4, 16 bits wide
  assign Z12 = _012 | A12 | B12 | C12 | D12 | P12;  // OR_Gate or_5, 16 bits wide
  assign Z1 = _01 | A1 | B1 | C1 | D1 | P1;  // OR_Gate or_6, 16 bits wide
  assign Z5 = _05 | A5 | B5 | C5 | D5 | P5;  // OR_Gate or_7, 16 bits wide
  assign Z9 = _09 | A9 | B9 | C9 | D9 | P9;  // OR_Gate or_8, 16 bits wide
  assign Z13 = _013 | A13 | B13 | C13 | D13 | P13;  // OR_Gate or_9, 16 bits wide
  Comparator #(.width(4)) comparator_19 (.a(HeadXPos), .b(AXPos), .eq(comparator_19_eq));  // open: gt, lt
  Comparator #(.width(4)) comparator_20 (.a(HeadYPos), .b(AYPos), .eq(comparator_20_eq));  // open: gt, lt
  Comparator #(.width(4)) comparator_21 (.a(HeadXPos), .b(BXPos), .eq(comparator_21_eq));  // open: gt, lt
  Comparator #(.width(4)) comparator_22 (.a(HeadYPos), .b(BYPos), .eq(comparator_22_eq));  // open: gt, lt
  Comparator #(.width(4)) comparator_23 (.a(HeadXPos), .b(CXPos), .eq(comparator_23_eq));  // open: gt, lt
  Comparator #(.width(4)) comparator_24 (.a(HeadYPos), .b(CYPos), .eq(comparator_24_eq));  // open: gt, lt
  Comparator #(.width(4)) comparator_25 (.a(HeadXPos), .b(DXPos), .eq(comparator_25_eq));  // open: gt, lt
  Comparator #(.width(4)) comparator_26 (.a(HeadYPos), .b(DYPos), .eq(comparator_26_eq));  // open: gt, lt
  and and_7 (and_7_out, comparator_19_eq, comparator_20_eq, Aup);
  and and_8 (and_8_out, comparator_21_eq, comparator_22_eq, Bup);
  and and_9 (and_9_out, comparator_23_eq, comparator_24_eq, Cup);
  and and_10 (and_10_out, comparator_25_eq, comparator_26_eq, Dup);
  assign Z2 = _02 | A2 | B2 | C2 | D2 | P2;  // OR_Gate or_10, 16 bits wide
  assign Z6 = _06 | A6 | B6 | C6 | D6 | P6;  // OR_Gate or_11, 16 bits wide
  assign Z10 = _010 | A10 | B10 | C10 | D10 | P10;  // OR_Gate or_12, 16 bits wide
  assign Z14 = _014 | A14 | B14 | C14 | D14 | P14;  // OR_Gate or_13, 16 bits wide
  Comparator #(.width(4)) comparator_27 (.a(State), .b(4'b1010), .eq(comparator_27_eq));  // open: gt, lt
  assign Z3 = _03 | A3 | B3 | C3 | D3 | P3;  // OR_Gate or_14, 16 bits wide
  and and_11 (tunnel[0], comparator_27_eq, tunnel[1]);
  or or_15 (or_15_out, and_7_out, and_8_out, and_9_out, and_10_out);
  assign Z7 = _07 | A7 | B7 | C7 | D7 | P7;  // OR_Gate or_16, 16 bits wide
  assign Z11 = _011 | A11 | B11 | C11 | D11 | P11;  // OR_Gate or_17, 16 bits wide
  assign Z15 = _015 | A15 | B15 | C15 | D15 | P15;  // OR_Gate or_18, 16 bits wide
  Clock clock_1 (.out(clock_1_out));
  and and_12 (CLK, clock_1_out, not_6_out);
  not not_6 (not_6_out, tunnel[1]);
  or or_19 (or_19_out, tunnel[1], or_15_out);
  Register #(.width(1)) register_1 (.D(or_19_out), .en(1'b1), .Q(tunnel[1]), .clk(CLK));  // open: clr

  // Notes on the sheet:
  //   Control
  //   a=1100001 x61
  //   d=1100100 x64
  //   s=1110011 x73
  //   w=1110111 x77
endmodule
